// Logisim project ex02.circ as structural Verilog: 1 circuit, main circuit main
module main (
  input  A,
  input  B,
  input  C_D,
  input  D,
  output out_5
);

  wire or_1_out, or_2_out;

  or or_1 (or_1_out, A, B);
  or or_2 (or_2_out, C_D, D);
  and and_1 (out_5, or_1_out, or_2_out);

  // Notes on the sheet:
  //   C
  //   A+B
endmodule
