// Logisim project ex03.circ as structural Verilog: 1 circuit, main circuit main
module main (
  input  in_1,
  input  in_2,
  input  in_3,
  input  in_4,
  output out_5
);

  wire and_1_out, nand_1_out, not_1_out;

  and and_1 (and_1_out, in_1, in_2);
  not not_1 (not_1_out, in_3);
  nand nand_1 (nand_1_out, in_3, in_4);
  or or_1 (out_5, and_1_out, not_1_out, nand_1_out);

  // Notes on the sheet:
  //   (a.b)
  //   c'
  //   (c'.d')
endmodule
