// Logisim project ex06.circ as structural Verilog: 1 circuit, main circuit main
module main (
  input  in_1,
  input  in_2,
  input  in_3,
  input  in_4,
  input  in_5,
  input  in_6,
  input  in_7,
  input  in_8,
  input  in_9,
  input  in_10,
  input  in_11,
  input  in_12,
  input  in_13,
  input  C05,
  input  in_15,
  output out_16,
  output out_17,
  output out_18,
  output out_19
);

  wire and_1_out, and_2_out, and_3_out, and_4_out, and_5_out, and_6_out, and_7_out, and_8_out, nor_1_out,
       nor_2_out, not_1_out, not_2_out, not_3_out, not_4_out, not_5_out, not_6_out, not_7_out, or_1_out;

  not not_1 (not_1_out, in_6);
  not not_2 (not_2_out, in_8);
  not not_3 (not_3_out, in_15);
  and and_1 (and_1_out, in_1, in_2);
  and and_2 (and_2_out, in_3, in_4);
  not not_4 (not_4_out, in_5);
  and and_3 (and_3_out, not_1_out, in_7);
  not not_5 (not_5_out, in_7);
  not not_6 (not_6_out, in_9);
  nor nor_1 (nor_1_out, in_12, in_13);
  nor nor_2 (nor_2_out, in_12, in_13, C05);
  or or_1 (or_1_out, and_2_out, not_4_out);
  and and_4 (and_4_out, not_5_out, in_6);
  and and_5 (and_5_out, in_8, not_6_out);
  and and_6 (and_6_out, not_2_out, in_9);
  and and_7 (and_7_out, nor_2_out, not_3_out);
  or or_2 (out_17, and_3_out, and_4_out);
  and and_8 (and_8_out, and_5_out, and_6_out);
  not not_7 (not_7_out, in_10);
  and and_9 (out_19, nor_1_out, and_7_out);
  and and_10 (out_16, and_1_out, or_1_out);
  or or_3 (out_18, and_8_out, not_7_out, in_11);

  // Notes on the sheet:
  //   C01
  //   C02
  //   C04
endmodule
